# Fritzing sketch Wiring_diagram_raw (saved by Fritzing 1.0.5)
breadboards: 2

parts:
  Part1 = SparkFun_ACS723_Current_Sensor_Breakout [part_number=13679]
  R1 = Resistor [tolerance=±5% power=0.25W resistance=220 package=THT]
  Part2 = MQ-7 breakout
  A1 = Hibiscus-sense-ESP32-WROOM-32
  U1 = Module 4 Relais 5V [package="Module 4 Relais 5V"]
  L298N1 = L298N DC motor driver
  F1 = Fan - Ventilador [package=THT]
  Part3 = KY-037 High Sensitivity Sound Detection Module [package="Breakout board"]
  S1 = Pushbutton [package="[THT]"]
  S2 = Pushbutton [package="[THT]"]
  S3 = Pushbutton [package="[THT]"]
  M1 = gear-motor
  R2 = Resistor [tolerance=±5% power=0.25W resistance=220 package=THT]
  R3 = Resistor [tolerance=±5% power=0.25W resistance=220 package=THT]
  J1 = Piezo Speaker  # not connected
  VCC1 = 4 x AAA Battery Mount [internal_resistance=0.1Ω]
  R4 = Resistor [tolerance=±5% power=0.25W resistance=220 package=THT]
  R5 = Resistor [tolerance=±5% power=0.25W resistance=220 package=THT]
  R6 = Resistor [tolerance=±5% power=0.25W resistance=220 package=THT]
  LED1 = LED - 5mm [color="Red (633nm)" current=0.030A package="5 mm [THT]"]
  LED2 = LEDs [package=led10mm]
  LED3 = LEDs [package=led10mm]
  A2 = Hibiscus-sense-ESP32-WROOM-32
  U2 = Module 4 Relais 5V [package="Module 4 Relais 5V"]
  LED4 = smd LED [color="Red (633nm)" package="0805 [SMD]"]
  A3 = Hibiscus-sense-ESP32-WROOM-32
  Part4 = SparkFun_ACS723_Current_Sensor_Breakout [part_number=13679]
  LED5 = LED - 5mm [color="Red (633nm)" current=0.030A package="5 mm [THT]"]
  A4 = DHT22 module
  R7 = Photocell (LDR) [power=0.25W dark_resistance_@0.01lx=300kΩ light_resistance_@100lx=400Ω luminance=10lx package=THT]

nets:
  VCC: Part1.VCC, Part3.+, A2.Pin_1, U2.VCC
  N1: Part1.2, A2.Pin_22
  GND: Part1.GND, Part3.G, A2.Pin_10, A2.Pin_16, A2.Pin_31, U2.GND
  N2: Part1.IP+, LED4.anode
  N3: Part1.IP-, U2.K4-NO
  VCC_2: R1.Pin_0, Part2.VCC, U1.VCC, R2.Pin_0, R3.Pin_0, A4.+
  N4: R1.Pin_1, A1.Pin_22, S3.Pin_3, S3.Pin_4
  GND_2: Part2.GND, U1.GND, S1.Pin_1, S1.Pin_2, S2.Pin_1, S2.Pin_2, S3.Pin_1, S3.Pin_2, A4.-, R7.pin_0
  N5: Part2.AO, A1.Pin_19
  N6: A1.Pin_20, S1.Pin_3, S1.Pin_4, R3.Pin_1
  N7: A1.Pin_21, S2.Pin_3, S2.Pin_4, R2.Pin_1
  N8: A1.Pin_23, U1.IN1
  N9: A1.Pin_24, U1.IN2
  N10: A1.Pin_25, U1.IN3
  N11: A1.Pin_26, L298N1.ENA
  N12: A1.Pin_27, L298N1.IN1
  N13: A1.Pin_28, L298N1.IN2
  N14: A1.Pin_29, A4.Out
  N15: A1.Pin_30, R7.pin_1
  5V: U1.K1-NF, U1.K2-NF, U1.K3-NF, L298N1.5V, F1.5V, VCC1.+
  N16: U1.K1-NO, R4.Pin_1
  N17: U1.K2-NO, R5.Pin_1
  N18: U1.K3-NO, R6.Pin_1
  N19: L298N1.OUT1, M1.pin_2
  N20: L298N1.OUT2, M1.pin_1
  12V: L298N1.12V, F1.GND, VCC1.-, LED1.cathode, LED2.C, LED3.C
  N21: Part3.D0, A2.Pin_7
  N22: R4.Pin_0, LED3.A
  N23: R5.Pin_0, LED2.A
  N24: R6.Pin_0, LED1.anode
  N25: A2.Pin_27, U2.IN1
  N26: A3.Pin_1, A3.Pin_17, Part4.VCC
  N27: A3.Pin_25, Part4.2
  N28: A3.Pin_32, Part4.GND
  N29: Part4.IP+, LED5.anode

custom parts:
  SparkFun_ACS723_Current_Sensor_Breakout: Description: The SparkFun Current Sensor Breakout is a high accuracy board that utilizes the ACS723 for moderate AC and DC current sensing applications. The ACS723 sensor uses a Hall effect sensor to output a voltage relative to the current flowing through the IP+ and IP- pins on the board. The advantage of using a Hall effect sensor, specifically, is that the circuit being sensed and the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
  MQ-7 breakout: SKU: 101282
  Hibiscus-sense-ESP32-WROOM-32: Hibiscus Sense – ESP32 Development Board.
  Module 4 Relais 5V: Module 4 Relais 5V 4x SPD-06VDC-SD-C
  L298N DC motor driver: 2x DC motor driver with 78M05 positive voltage regulator (7..35 V) L298N: max 46 V, 2 A Set 5 V Enable jumper to enable 5 V regultor (needed for the L298N) and +5 V output at screw terminal or supply external +5 V at screw terminal Set ENA and/or ENB to +5 V to enable motor permanently or supply ENA and/or ENB with PWM signal IN1 and IN2 set rotation directory for motor A (OUT1/OUT2) IN2 and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
  Fan - Ventilador: Ventilador de 2 pines, se encuentra comunmente en computadoras de escritorio
  KY-037 High Sensitivity Sound Detection Module: KY-037 high sensitivity sound detection module is an analog/digital sensor that uses a condenser microphone to observe changes in environment noise.
  DHT22 module: DHT22 module. Pins VCC Data GND.
